// Logisim project pratica_arq.circ as structural Verilog: 6 circuits, main circuit main
module main (
  input  [1:0] in_1,
  input  [1:0] in_2,
  input  [1:0] in_3,
  input  in_4,
  input  in_5
);

  wire AluSrc, and_1_out, branch, clk, if_1_p4, MemRead, MemRead_1, MemToReg, MemToReg_1, MemWrite,
       MemWrite_1, RegDst, register_1_q, register_2_q, register_3_q, register_4_q, register_13_q,
       register_16_q, RegWrite, RegWrite_1, Zero;
  wire [1:0] AluOP_1, AluOP_2;
  wire [3:0] AluOP, control_unit_1_p9;
  wire [4:0] register_7_q, register_17_q, RW, RW_1, SA, ShiftA;
  wire [5:0] Funct, Funct_1, op;
  wire [31:0] A, A_1, B, B_1, BReg, BReg_1, C_1, C_2, C_3, C_4, D, D_1, IF_ID_q, j_val, mipsprogramrom_1_p1,
       multiplexer_1_out, multiplexer_2_out, multiplexer_3_out, multiplexer_4_out, register_10_q, W;

  Clock clock_1 (.out(clk));
  Multiplexer #(.width(32), .enable("false")) multiplexer_1 (
    .in0({32{1'b0}}), .in1(j_val), .out(multiplexer_1_out), .sel(and_1_out));
  and and_1 (and_1_out, branch, Zero);
  // IF if_1: pin names not known; wires that end beside it: multiplexer_1_out, clk, in_4, if_1_p4, if_1_p4
  // MIPSProgramROM mipsprogramrom_1: pin names not known; wires that end beside it: mipsprogramrom_1_p1
  Register #(.width(32)) IF_ID (.D(mipsprogramrom_1_p1), .en(1'b1), .clk(clk), .Q(IF_ID_q), .clr(in_4));
  Register #(.width(1)) register_1 (.D(RegWrite_1), .en(1'b1), .clk(clk), .Q(register_1_q), .clr(in_4));
  Register #(.width(1)) register_2 (.D(MemRead_1), .en(1'b1), .clk(clk), .Q(register_2_q), .clr(in_4));
  Register #(.width(1)) register_3 (.D(MemWrite_1), .en(1'b1), .clk(clk), .Q(register_3_q), .clr(in_4));
  Register #(.width(1)) register_4 (.D(MemToReg_1), .en(1'b1), .clk(clk), .Q(register_4_q), .clr(in_4));
  Register #(.width(2)) register_5 (.D(AluOP_1), .en(1'b1), .clk(clk), .Q(AluOP_2), .clr(in_4));
  Register #(.width(6)) register_6 (.D(Funct_1), .en(1'b1), .clk(clk), .Q(Funct), .clr(in_4));
  Register #(.width(5)) register_7 (.D(RW_1), .en(1'b1), .clk(clk), .Q(register_7_q), .clr(in_4));
  Register #(.width(32)) register_8 (.D(A_1), .en(1'b1), .clk(clk), .Q(A), .clr(in_4));
  Register #(.width(32)) register_9 (.D(B_1), .en(1'b1), .clk(clk), .Q(B), .clr(in_4));
  Register #(.width(32)) register_10 (.D(BReg_1), .en(1'b1), .clk(clk), .Q(register_10_q), .clr(in_4));
  Register #(.width(32)) register_11 (.D(C_1), .en(1'b1), .clk(clk), .Q(C_2), .clr(in_4));
  Register #(.width(32)) register_12 (.D(D_1), .en(1'b1), .clk(clk), .Q(D), .clr(in_4));
  Register #(.width(1)) register_13 (.D(register_1_q), .en(1'b1), .clk(clk), .Q(register_13_q), .clr(in_4));
  Register #(.width(1)) register_14 (.D(register_2_q), .en(1'b1), .clk(clk), .Q(MemRead), .clr(in_4));
  Register #(.width(1)) register_15 (.D(register_3_q), .en(1'b1), .clk(clk), .Q(MemWrite), .clr(in_4));
  Register #(.width(1)) register_16 (.D(register_4_q), .en(1'b1), .clk(clk), .Q(register_16_q), .clr(in_4));
  Register #(.width(5)) register_17 (.D(register_7_q), .en(1'b1), .clk(clk), .Q(register_17_q), .clr(in_4));
  Register #(.width(32)) register_18 (.D(register_10_q), .en(1'b1), .clk(clk), .Q(BReg), .clr(in_4));
  Register #(.width(32)) register_19 (.D(C_2), .en(1'b1), .clk(clk), .Q(C_3), .clr(in_4));
  // Control_Unit control_unit_1: pin names not known; wires that end beside it: IF_ID_q, RegDst, AluSrc, MemToReg_1, RegWrite_1, MemRead_1, MemWrite_1, branch, control_unit_1_p9
  Register #(.width(1)) register_20 (.D(register_13_q), .en(1'b1), .clk(clk), .Q(RegWrite), .clr(in_4));
  Register #(.width(1)) register_21 (.D(register_16_q), .en(1'b1), .clk(clk), .Q(MemToReg), .clr(in_4));
  Register #(.width(5)) register_22 (.D(register_17_q), .en(1'b1), .clk(clk), .Q(RW), .clr(in_4));
  ID id_1 (
    .W(W), .CLK(clk), .RegWriter(RegWrite), .AluSrc(AluSrc), .RW(RW), .code(IF_ID_q), .RegDst(RegDst),
    .A(A_1), .BReg(BReg_1), .B(B_1), .op(op), .RW_1(RW_1), .j_val(j_val), .Funct(Funct_1), .SA(ShiftA));
  Register #(.width(4)) register_23 (.D(control_unit_1_p9), .en(1'b1), .clk(clk), .Q(AluOP), .clr(in_4));
  Multiplexer #(.select(2), .width(32), .enable("false")) multiplexer_2 (
    .in0(A), .in1(C_2), .in2(C_3), .out(multiplexer_2_out), .sel(in_1));  // open: in3
  Multiplexer #(.select(2), .width(32), .enable("false")) multiplexer_3 (
    .in0(B), .in1(C_2), .in2(C_3), .out(multiplexer_3_out), .sel(in_3));  // open: in3
  EX ex_1 (.A(multiplexer_2_out), .B(multiplexer_3_out), .AluOP(AluOP), .SA(SA), .Zero(Zero), .C(C_1));
  Multiplexer #(.select(2), .width(32), .enable("false")) multiplexer_4 (
    .in0(BReg), .in1(C_3), .in2(C_4), .out(multiplexer_4_out), .sel(in_2));  // open: in3
  MEM mem_1 (
    .Addr(C_2), .Data(multiplexer_4_out), .MemWrite(MemWrite), .RST(in_4), .Sel(4'b1111), .MemRead(MemRead),
    .CLK(clk), .D(D_1));
  WB wb_1 (.ALU(C_3), .MEM(D), .MemToReg(MemToReg), .W(W));
  Register #(.width(32)) register_24 (.D(W), .en(1'b1), .clk(clk), .Q(C_4), .clr(in_4));

  // Other names for the same wires on the sheet: rst = in_4

  // Notes on the sheet:
  //   contents of mipsprogramrom_1 (hex, n*v repeats v):
  //   addu $9, $11, $12 subu $10, $9, $8 j 4 sw $9, 0x0000($0) bne $8, $9, 12 lw $10, 0x0000($0) lw $11,
  //   0x0001($0)
  //   ID/EX
  //   EX/ME
  //   ME/WB
endmodule

module PC (
  input  WE,
  input  CLK,
  input  RST,
  input  [31:0] j_val,
  input  branch,
  output [31:0] PC
);

  wire [31:0] adder_1_out, multiplexer_1_out;

  Register #(.width(32)) IF_MAIN (.D(multiplexer_1_out), .en(WE), .clk(CLK), .Q(PC), .clr(RST));
  Adder #(.width(32)) adder_1 (.a(PC), .b(32'h4), .out(adder_1_out));  // open: cin, cout
  Multiplexer #(.width(32), .enable("false")) multiplexer_1 (
    .in0(adder_1_out), .in1(j_val), .out(multiplexer_1_out), .sel(branch));
endmodule

module ID (
  input  [31:0] W,
  input  CLK,
  input  RegWriter,
  input  AluSrc,
  input  [4:0] RW,
  input  [31:0] code,
  input  RegDst,
  output [31:0] A,
  output [31:0] BReg,
  output [31:0] B,
  output [5:0] op,
  output [4:0] RW_1,
  output [31:0] j_val,
  output [5:0] Funct,
  output [4:0] SA
);

  wire [31:0] bit_extender_1_out;

  Multiplexer #(.width(5), .enable("false")) multiplexer_1 (
    .in0(code[20:16]), .in1(code[15:11]), .out(RW_1), .sel(RegDst));
  // RegisterFile registerfile_1: pin names not known; wires that end beside it: W, CLK, RegWriter, RW, code[25:21], code[20:16], A, BReg
  Multiplexer #(.width(32), .enable("false")) multiplexer_2 (
    .in0(BReg), .in1(bit_extender_1_out), .out(B), .sel(AluSrc));
  assign bit_extender_1_out = {{16{code[15]}}, code[15:0]};  // Bit_Extender bit_extender_1
  Shifter #(.width(32)) shifter_1 (.in(bit_extender_1_out), .\dist (5'b00010), .out(j_val));

  assign Funct = code[5:0];
  assign op = code[31:26];
  assign SA = code[10:6];
endmodule

module EX (
  input  [31:0] A,
  input  [31:0] B,
  input  [3:0] AluOP,
  input  [4:0] SA,
  output Zero,
  output [31:0] C
);

  // Mips_ALU mips_alu_1: pin names not known; wires that end beside it: A, B, AluOP, SA, Zero, C
endmodule

module MEM (
  input  [31:0] Addr,
  input  [31:0] Data,
  input  MemWrite,
  input  RST,
  input  [3:0] Sel,
  input  MemRead,
  input  CLK,
  output [31:0] D
);

  // MIPS_RAM mips_ram_1: pin names not known; wires that end beside it: Addr[19:0], Data, MemWrite, Sel, CLK, MemRead, RST, D
endmodule

module WB (
  input  [31:0] ALU,
  input  [31:0] MEM,
  input  MemToReg,
  output [31:0] W
);

  Multiplexer #(.width(32), .enable("false")) multiplexer_1 (.in0(ALU), .in1(MEM), .out(W), .sel(MemToReg));
endmodule
