// Logisim project test.circ as structural Verilog: 6 circuits, main circuit main
module main (
  input  in_1
);

  wire clock_1_out, comparator_1_eq, control_unit_1_p3, control_unit_1_p4, control_unit_1_p5,
       control_unit_1_p6, control_unit_1_p7, control_unit_1_p8, control_unit_1_p9, control_unit_1_p10,
       ex_mem_1_p10, ex_mem_1_p11, ex_mem_1_p12, ex_mem_1_p13, ex_mem_1_p15, ex_mem_1_p16, hazard_unit_1_p3,
       hazard_unit_1_p4, id_ex_1_p17, id_ex_1_p18, id_ex_1_p19, id_ex_1_p20, id_ex_1_p21, id_ex_1_p22,
       id_ex_1_p23, id_ex_1_p29, if_id_1_p3, instsplit_1_p2, instsplit_1_p3, instsplit_1_p4, instsplit_1_p5,
       instsplit_1_p6, instsplit_1_p7, Jmp, mem_wb_1_p9, mips_alu_1_p5, mips_ram_1_p7, mipsprogramrom_1_p1,
       mipsprogramrom_1_p3, not_1_out, not_3_out, undriven, undriven_2, WE;
  wire [1:0] undriven_3, undriven_4;
  wire [4:0] hazard_unit_1_p5, id_ex_1_p28, multiplexer_2_out, RW;
  wire [15:0] instsplit_1_p8;
  wire [31:0] adder_1_out, adder_2_out, bit_extender_1_out, C_2, C_3, ex_mem_1_p14, id_ex_1_p24, id_ex_1_p25,
       id_ex_1_p30, if_id_1_p5, mem_wb_1_p10, mem_wb_1_p11, multiplexer_1_out, multiplexer_3_out,
       multiplexer_4_out, multiplexer_5_out, register_1_q, registerfile_1_p6, registerfile_1_p7,
       shifter_1_out, W;

  Multiplexer #(.width(32), .enable("false")) multiplexer_1 (
    .in0(adder_1_out), .in1(adder_2_out), .out(multiplexer_1_out), .sel(Jmp));
  not not_1 (not_1_out, undriven);
  Clock clock_1 (.out(clock_1_out));
  Register #(.width(32)) register_1 (
    .D(multiplexer_1_out), .en(not_1_out), .clk(clock_1_out), .Q(register_1_q), .clr(in_1));
  Adder #(.width(32)) adder_1 (.a(register_1_q), .b(32'h4), .out(adder_1_out));  // open: cin, cout
  // MIPSProgramROM mipsprogramrom_1: pin names not known; wires that end beside it: mipsprogramrom_1_p1, mipsprogramrom_1_p1, mipsprogramrom_1_p3
  // IF_ID if_id_1: pin names not known; wires that end beside it: adder_1_out, clock_1_out, if_id_1_p3, Jmp, if_id_1_p5
  not not_2 (if_id_1_p3, undriven_2);
  // InstSplit instsplit_1: pin names not known; wires that end beside it: mipsprogramrom_1_p3, instsplit_1_p2, instsplit_1_p3, instsplit_1_p4, instsplit_1_p5, instsplit_1_p6, instsplit_1_p7, instsplit_1_p8, clock_1_out
  assign bit_extender_1_out = {{16{instsplit_1_p8[15]}}, instsplit_1_p8};  // Bit_Extender bit_extender_1
  // Control_Unit control_unit_1: pin names not known; wires that end beside it: instsplit_1_p2, instsplit_1_p3, control_unit_1_p3, control_unit_1_p4, control_unit_1_p5, control_unit_1_p6, control_unit_1_p7, control_unit_1_p8, control_unit_1_p9, control_unit_1_p10
  // RegisterFile registerfile_1: pin names not known; wires that end beside it: W, WE, RW, instsplit_1_p4, instsplit_1_p5, registerfile_1_p6, registerfile_1_p7
  Shifter #(.width(32)) shifter_1 (.in(bit_extender_1_out), .\dist (5'b00010), .out(shifter_1_out));
  Comparator #(.width(32)) comparator_1 (
    .a(registerfile_1_p6), .b(registerfile_1_p7), .eq(comparator_1_eq));  // open: gt, lt
  Adder #(.width(32)) adder_2 (.a(shifter_1_out), .b(if_id_1_p5), .out(adder_2_out));  // open: cin, cout
  // Hazard_Unit hazard_unit_1: pin names not known; wires that end beside it: instsplit_1_p4, instsplit_1_p5, hazard_unit_1_p3, hazard_unit_1_p4, hazard_unit_1_p5
  and and_1 (Jmp, control_unit_1_p10, comparator_1_eq);
  // ID_EX id_ex_1: pin names not known; wires that end beside it: control_unit_1_p3, control_unit_1_p4, control_unit_1_p5, control_unit_1_p6, control_unit_1_p7, control_unit_1_p8, control_unit_1_p9, registerfile_1_p6, registerfile_1_p7, instsplit_1_p4, instsplit_1_p5, instsplit_1_p6, instsplit_1_p7, bit_extender_1_out, clock_1_out, hazard_unit_1_p3, id_ex_1_p17, id_ex_1_p18, id_ex_1_p19, id_ex_1_p20, id_ex_1_p21, id_ex_1_p22, id_ex_1_p23, id_ex_1_p24, id_ex_1_p25, hazard_unit_1_p4, hazard_unit_1_p5, id_ex_1_p28, id_ex_1_p29, id_ex_1_p30
  Multiplexer #(.width(5), .enable("false")) multiplexer_2 (
    .in0(hazard_unit_1_p5), .in1(id_ex_1_p28), .out(multiplexer_2_out), .sel(id_ex_1_p23));
  Multiplexer #(.select(2), .width(32), .enable("false")) multiplexer_3 (
    .in0(id_ex_1_p24), .in1(C_2), .in2(C_3), .out(multiplexer_3_out), .sel(undriven_4));  // open: in3
  Multiplexer #(.select(2), .width(32), .enable("false")) multiplexer_4 (
    .in0(id_ex_1_p25), .in1(C_2), .in2(C_3), .out(multiplexer_4_out), .sel(undriven_3));  // open: in3
  Multiplexer #(.width(32), .enable("false")) multiplexer_5 (
    .in0(multiplexer_4_out), .in1(id_ex_1_p30), .out(multiplexer_5_out), .sel(id_ex_1_p22));
  // Mips_ALU mips_alu_1: pin names not known; wires that end beside it: multiplexer_3_out, multiplexer_5_out, id_ex_1_p21, id_ex_1_p29, mips_alu_1_p5
  // EX_MEM ex_mem_1: pin names not known; wires that end beside it: id_ex_1_p17, id_ex_1_p18, id_ex_1_p19, id_ex_1_p20, mips_alu_1_p5, multiplexer_5_out, multiplexer_2_out, clock_1_out, in_1, ex_mem_1_p10, ex_mem_1_p11, ex_mem_1_p12, ex_mem_1_p13, ex_mem_1_p14, ex_mem_1_p15, ex_mem_1_p16
  // MIPS_RAM #(.addrWidth(24)) mips_ram_1: pin names not known; wires that end beside it: ex_mem_1_p14[23:0], ex_mem_1_p15, ex_mem_1_p12, 4'b1111, clock_1_out, ex_mem_1_p13, mips_ram_1_p7
  // MEM_WB mem_wb_1: pin names not known; wires that end beside it: ex_mem_1_p10, ex_mem_1_p11, mips_ram_1_p7, ex_mem_1_p14, ex_mem_1_p16, clock_1_out, in_1, WE, mem_wb_1_p9, mem_wb_1_p10, mem_wb_1_p11, RW
  not not_3 (not_3_out, mem_wb_1_p9);
  Multiplexer #(.width(32), .enable("false")) multiplexer_6 (
    .in0(mem_wb_1_p10), .in1(mem_wb_1_p11), .out(W), .sel(not_3_out));

  // Other names for the same wires on the sheet: rst = in_1

  // Notes on the sheet:
  //   contents of mipsprogramrom_1 (hex, n*v repeats v):
  //   addu $8, $9, $10 addu $9, $11, $12 subu $10, $9, $8 sll $5, $5, 2 j 12 sw $9, 0x0000($0) bne $8, $9,
  //   12 lw $10, 0x0000($0) lw $11, 0x0001($0)
endmodule

module PC (
  input  WE,
  input  CLK,
  input  RST,
  input  [31:0] j_val,
  input  branch,
  output [31:0] PC
);

  wire [31:0] adder_1_out, multiplexer_1_out;

  Register #(.width(32)) IF_MAIN (.D(multiplexer_1_out), .en(WE), .clk(CLK), .Q(PC), .clr(RST));
  Adder #(.width(32)) adder_1 (.a(PC), .b(32'h4), .out(adder_1_out));  // open: cin, cout
  Multiplexer #(.width(32), .enable("false")) multiplexer_1 (
    .in0(adder_1_out), .in1(j_val), .out(multiplexer_1_out), .sel(branch));
endmodule

module ID (
  input  [31:0] W,
  input  CLK,
  input  RegWriter,
  input  AluSrc,
  input  [4:0] RW,
  input  [31:0] code,
  input  RegDst,
  output [31:0] A,
  output [31:0] BReg,
  output [31:0] B,
  output [5:0] op,
  output [4:0] RW_1,
  output [31:0] j_val,
  output [5:0] Funct,
  output [4:0] SA
);

  wire [31:0] bit_extender_1_out;

  Multiplexer #(.width(5), .enable("false")) multiplexer_1 (
    .in0(code[20:16]), .in1(code[15:11]), .out(RW_1), .sel(RegDst));
  // RegisterFile registerfile_1: pin names not known; wires that end beside it: W, CLK, RegWriter, RW, code[25:21], code[20:16], A, BReg
  Multiplexer #(.width(32), .enable("false")) multiplexer_2 (
    .in0(BReg), .in1(bit_extender_1_out), .out(B), .sel(AluSrc));
  assign bit_extender_1_out = {{16{code[15]}}, code[15:0]};  // Bit_Extender bit_extender_1
  Shifter #(.width(32)) shifter_1 (.in(bit_extender_1_out), .\dist (5'b00010), .out(j_val));

  assign Funct = code[5:0];
  assign op = code[31:26];
  assign SA = code[10:6];
endmodule

module EX (
  input  [31:0] A,
  input  [31:0] B,
  input  [3:0] AluOP,
  input  [4:0] SA,
  output Zero,
  output [31:0] C
);

  // Mips_ALU mips_alu_1: pin names not known; wires that end beside it: A, B, AluOP, SA, Zero, C
endmodule

module MEM (
  input  [31:0] Addr,
  input  [31:0] Data,
  input  MemWrite,
  input  RST,
  input  [3:0] Sel,
  input  MemRead,
  input  CLK,
  output [31:0] D
);

  // MIPS_RAM mips_ram_1: pin names not known; wires that end beside it: Addr[19:0], Data, MemWrite, Sel, CLK, MemRead, RST, D
endmodule

module WB (
  input  [31:0] ALU,
  input  [31:0] MEM,
  input  MemToReg,
  output [31:0] W
);

  Multiplexer #(.width(32), .enable("false")) multiplexer_1 (.in0(ALU), .in1(MEM), .out(W), .sel(MemToReg));
endmodule
